# Fritzing sketch wiring (saved by Fritzing 0.9.3b)
breadboards: 1

parts:
  MOTOR1 = 28BYJ-48 Stepper Motor
  X1 = X113647 Stepper Driver Board [part_number=X113647 package=board]
  Part1 = Arduino Uno (Rev3)
  Part2 = Breakout Board for Electret Microphone

nets (from the breadboard view):
  N1: MOTOR1.BLUE, X1.BLUE
  N2: MOTOR1.PINK, X1.PINK
  N3: MOTOR1.RED, X1.YELLOW
  N4: MOTOR1.ORANGE, X1.ORANGE
  N5: MOTOR1.YELLOW, X1.RED
  N6: X1.IN1, Part1.D2
  N7: X1.IN2, Part1.D3_PWM
  N8: X1.IN3, Part1.D4
  N9: X1.IN4, Part1.D5_PWM
  GND: X1.GND, Part1.GND, Part2.GND
  5V: X1.+V, Part1.5V, Part2.VCC
  N10: Part1.D7, Part2.AUD

custom parts:
  28BYJ-48 Stepper Motor: 28BYJ-48 gear-reduction stepper motor (small)
  X113647 Stepper Driver Board: A common stepper motor driver board based on ULN2003APG darlington array
